// Logisim project CPU.circ as structural Verilog: 1 circuit, main circuit main
// CPU
module main (
  input  [31:0] INSTRUCTION,
  input  [23:0] CURRENT_PC,
  input  CQ_PASSED,
  input  [31:0] REG_1_VAL,
  input  [31:0] REG_2_VAL,
  input  [31:0] REG_3_VAL,
  input  [31:0] ALU_RESULT,
  input  [31:0] MEM_OUT,
  output [23:0] JUMP_ADDRESS,
  output [2:0] CQ_QUERY,
  output CR_WRITE,
  output [3:0] REG_1_READ,
  output [3:0] REG_2_READ,
  output [3:0] REG_3_WRITE,
  output [31:0] REG_WRITE_VAL,
  output REG_WRITE,
  output [31:0] ALU_SOURCE_X,
  output [31:0] ALU_SOURCE_Y,
  output [3:0] ALU_OPERATION,
  output [23:0] MEM_ADDR,
  output [31:0] MEM_IN,
  output SHL,
  output SHR,
  output AND,
  output IOR,
  output XOR,
  output STU,
  output MUL,
  output DIV,
  output SUB,
  output ADD,
  output MLD,
  output MST,
  output STL,
  output LNK,
  output JMP,
  output MEM_WRITE
);

  wire ALUSrc_out, and_1_out, MemtoReg, not_2_out, not_3_out, not_4_out, not_5_out, nPC_sel, RegWrite_out;
  wire [0:0] ExtOp_out;
  wire [31:0] bit_extender_2_out, bit_extender_3_out, bit_extender_4_out, LNK_O, PC_32, RI_OUT;

  Multiplexer #(.width(32), .enable("false")) multiplexer_1 (
    .in0(REG_2_VAL), .in1(RI_OUT), .out(ALU_SOURCE_Y), .sel(INSTRUCTION[24]));
  assign PC_32 = {{8{CURRENT_PC[23]}}, CURRENT_PC};  // Bit_Extender bit_extender_1
  Multiplexer #(.width(4), .enable("false")) multiplexer_2 (
    .in0(INSTRUCTION[3:0]), .in1(INSTRUCTION[19:16]), .out(REG_2_READ), .sel(ALUSrc_out));
  assign bit_extender_2_out = {{16{INSTRUCTION[15]}}, INSTRUCTION[15:0]};  // Bit_Extender bit_extender_2
  assign bit_extender_3_out = {{12{INSTRUCTION[19]}}, INSTRUCTION[19:0]};  // Bit_Extender bit_extender_3
  assign bit_extender_4_out = {{8{INSTRUCTION[23]}}, INSTRUCTION[23:0]};  // Bit_Extender bit_extender_4
  Multiplexer #(.select(2), .width(32), .enable("false")) multiplexer_3 (
    .in0(ALU_RESULT), .in1(MEM_OUT), .in2(LNK_O), .out(REG_WRITE_VAL), .sel({LNK, MemtoReg}));  // open: in3
  Adder #(.width(32)) adder_1 (.a(PC_32), .b(RI_OUT), .out(LNK_O));  // open: cin, cout
  Multiplexer #(.width(4), .enable("false")) multiplexer_4 (
    .in0(INSTRUCTION[19:16]), .in1(INSTRUCTION[3:0]), .out(REG_1_READ), .sel(and_1_out));
  and and_1 (and_1_out, ALUSrc_out, ~INSTRUCTION[24]);  // AND_Gate
  Multiplexer #(.width(32), .enable("false")) multiplexer_5 (
    .in0(ALU_RESULT), .out(MEM_IN), .sel(MEM_WRITE));  // open: in1
  Multiplexer #(.select(2), .width(32), .enable("false")) multiplexer_6 (
    .in0(bit_extender_2_out), .in1(bit_extender_3_out), .in2(bit_extender_4_out), .out(RI_OUT),
    .sel({JMP, ExtOp_out[0]}));  // open: in3
  Multiplexer #(.width(24), .enable("false")) multiplexer_7 (
    .in1(INSTRUCTION[23:0]), .out(JUMP_ADDRESS), .sel(nPC_sel));  // open: in0
  or ALUSrc (ALUSrc_out, STU, SUB, STL, LNK);
  not not_1 (REG_WRITE, RegWrite_out);
  or RegWrite (RegWrite_out, MST, CR_WRITE, JMP);
  not not_2 (not_2_out, INSTRUCTION[28]);
  not not_3 (not_3_out, INSTRUCTION[29]);
  not not_4 (not_4_out, INSTRUCTION[30]);
  not not_5 (not_5_out, INSTRUCTION[31]);
  buf MemWrite (MEM_WRITE, MST);  // OR_Gate
  buf u_MemtoReg (MemtoReg, MLD);  // OR_Gate
  buf u_nPC_sel (nPC_sel, JMP);  // OR_Gate
  or ExtOp (ExtOp_out[0], STL, CR_WRITE, LNK);
  and u_SHL (SHL, not_2_out, not_3_out, not_4_out, not_5_out);
  and u_SHR (SHR, INSTRUCTION[28], not_3_out, not_4_out, not_5_out);
  and AND_2 (AND, not_2_out, INSTRUCTION[28], not_4_out, not_5_out);
  and u_IOR (IOR, INSTRUCTION[28], INSTRUCTION[29], not_4_out, not_5_out);
  and u_XOR (XOR, not_2_out, not_3_out, INSTRUCTION[30], not_5_out);
  and u_STU (STU, INSTRUCTION[28], not_4_out, INSTRUCTION[30], not_5_out);
  and u_MUL (MUL, not_2_out, INSTRUCTION[29], INSTRUCTION[30], not_5_out);
  and u_DIV (DIV, INSTRUCTION[28], INSTRUCTION[29], INSTRUCTION[30], not_5_out);
  and u_SUB (SUB, not_2_out, not_3_out, not_4_out, INSTRUCTION[31]);
  and u_MLD (MLD, not_2_out, INSTRUCTION[29], not_4_out, INSTRUCTION[31]);
  and u_ADD (ADD, INSTRUCTION[28], not_3_out, not_4_out, INSTRUCTION[31]);
  and u_MST (MST, INSTRUCTION[28], not_3_out, not_4_out, INSTRUCTION[31]);
  and u_STL (STL, not_2_out, not_4_out, INSTRUCTION[30], INSTRUCTION[31]);
  and CMP (CR_WRITE, INSTRUCTION[28], not_3_out, INSTRUCTION[30], INSTRUCTION[31]);
  and u_LNK (LNK, not_2_out, INSTRUCTION[29], INSTRUCTION[30], INSTRUCTION[31]);
  and u_JMP (JMP, INSTRUCTION[28], INSTRUCTION[29], INSTRUCTION[30], INSTRUCTION[31]);

  assign ALU_OPERATION = INSTRUCTION[31:28];
  assign ALU_SOURCE_X = REG_1_VAL;
  assign CQ_QUERY = INSTRUCTION[27:25];
  assign MEM_ADDR = CURRENT_PC;
  assign REG_3_WRITE = INSTRUCTION[23:20];

  // Other names for the same wires on the sheet: CMP = CR_WRITE; RI[3:0] = INSTRUCTION[3:0];
  //   IMM[11:0] = INSTRUCTION[15:4]; RS[3:0] = INSTRUCTION[19:16]; RD[3:0] = INSTRUCTION[23:20];
  //   IS_RI = INSTRUCTION[24]; _CQ[2:0] = INSTRUCTION[27:25]; OP_Code[3:0] = INSTRUCTION[31:28]; memStore = MEM_WRITE

  // Notes on the sheet:
  //   INSTRUCTION MODULE
  //   CR MODULE
  //   REGISTER FILE MODULE
  //   ALU MODULE
  //   MEMORY MODULE
endmodule
