// Logisim project NPC.circ as structural Verilog: 1 circuit, main circuit main
// NPC
module main (
  input  CQ_PASSED,
  input  [31:0] INSTRUCTION,
  input  [23:0] CURRENT_PC,
  input  [23:0] JUMP_ADDRESS,
  output [23:0] NEXT_PC
);

  wire clk, Jump_Cmd, not_2_out, prev_jump, register_1_q;
  wire [23:0] adder_1_out, bit_extender_1_out, Immediate_Value, multiplexer_1_out, nextPC;
  wire [31:0] current_inst, inst;

  Register #(.width(1)) register_1 (.D(Jump_Cmd), .Q(register_1_q), .clk(clk));  // open: en, clr
  not not_1 (prev_jump, register_1_q);
  Register #(.width(32)) Instruction_Register (.D(inst), .Q(current_inst), .clk(clk));  // open: en, clr
  assign bit_extender_1_out = {{23{1'b0}}, 1'b1};  // Bit_Extender bit_extender_1
  Adder #(.width(24)) adder_1 (.a(bit_extender_1_out), .b(nextPC), .out(adder_1_out));  // open: cin, cout
  not not_2 (not_2_out, Jump_Cmd);
  Multiplexer #(.width(24), .enable("false")) multiplexer_1 (
    .in0(Immediate_Value), .in1(adder_1_out), .out(multiplexer_1_out), .sel(not_2_out));
  Register #(.width(24)) pc (.D(multiplexer_1_out), .Q(nextPC), .clk(clk));  // open: en, clr

  // Notes on the sheet:
  //   NPC MODULE
endmodule
